// Logisim project A 12-bit Custom RISC-V Microprocessor Datapath.circ as structural Verilog: 4 circuits, main circuit DataPath
module DataPath (
  input  Clock,
  output [11:0] Jump_Address,
  output [11:0] Data_1,
  output [11:0] Next_Inst_Address,
  output [8:0] Jump___Target,
  output [11:0] Data_2,
  output [11:0] Result___MEM_Data,
  output [11:0] Result___Addr_Lw___Sw,
  output [2:0] OP_Code,
  output [2:0] RS,
  output [2:0] RT,
  output [2:0] RD_Imm,
  output C_overflow,
  output Zero_Detector,
  output [11:0] Store_Data,
  output Load,
  output Store,
  output Beq_control,
  output RAM_to_REG
);

  wire and_1_out, control_unit_1_alu_src, control_unit_1_jump_control, control_unit_1_rt_rd,
       control_unit_1_sub, control_unit_1_write_enb, or_1_out, Reset_2_out, Reset_3_out, Reset_out;
  wire [2:0] multiplexer_2_out;
  wire [11:0] adder_2_out, bit_extender_1_out, multiplexer_1_out, multiplexer_3_out, ram_1_data, register_1_q;

  Multiplexer #(.width(12)) multiplexer_1 (
    .in0(multiplexer_3_out), .in1({Jump_Address[11:9], Jump___Target}), .out(multiplexer_1_out),
    .sel(control_unit_1_jump_control));  // open: en
  Register #(.width(12)) register_1 (
    .D(multiplexer_1_out), .Q(register_1_q), .clk(Clock), .clr(Reset_out));  // open: en
  Button Reset (.out(Reset_out));
  Adder #(.width(12)) adder_1 (
    .a(12'h1), .b(register_1_q), .out({Jump_Address[11:9], Next_Inst_Address[8:0]}), .cin(1'b0));  // open: cout
  // Probe on {Jump_Address[11:9], Next_Inst_Address[8:0]}
  ROM #(.addrWidth(12), .dataWidth(12)) rom_1 (.addr(register_1_q), .data({OP_Code, Jump___Target}));  // open: sel
  Control_Unit control_unit_1 (
    .ALU_OP(OP_Code), .RT_RD(control_unit_1_rt_rd), .Write_Enb(control_unit_1_write_enb),
    .ALU_Src(control_unit_1_alu_src), .Sub(control_unit_1_sub), .Store_enb(Store), .RAM_to_Reg(RAM_to_REG),
    .Jump_Control(control_unit_1_jump_control), .Load_enb(Load), .Beq_Control(Beq_control));
  // Probe on Jump___Target
  // Probe on {Jump_Address[11:9], Jump___Target}
  Multiplexer #(.width(3)) multiplexer_2 (
    .in0(Jump___Target[5:3]), .in1(Jump___Target[2:0]), .out(multiplexer_2_out), .sel(control_unit_1_rt_rd));  // open: en
  assign bit_extender_1_out = {{9{1'b0}}, Jump___Target[2:0]};  // Bit_Extender bit_extender_1
  Adder #(.width(12)) adder_2 (
    .a({Jump_Address[11:9], Next_Inst_Address[8:0]}), .b(bit_extender_1_out), .out(adder_2_out), .cin(1'b0));  // open: cout
  Button Reset_2 (.out(Reset_2_out));
  Register_File_12_bit register_file_12_bit_1 (
    .Write_Data(Result___MEM_Data), .Read_Data_1(Data_1), .Read_Data_2(Store_Data),
    .Enable(control_unit_1_write_enb), .Clock(Clock), .Reset(Reset_2_out), .RD(multiplexer_2_out),
    .RS(Jump___Target[8:6]), .RT(Jump___Target[5:3]));
  Multiplexer #(.width(12)) multiplexer_3 (
    .in0({Jump_Address[11:9], Next_Inst_Address[8:0]}), .in1(adder_2_out), .out(multiplexer_3_out),
    .sel(and_1_out));  // open: en
  and and_1 (and_1_out, Beq_control, Zero_Detector);
  Multiplexer #(.width(12)) multiplexer_4 (
    .in0(Store_Data), .in1(bit_extender_1_out), .out(Data_2), .sel(control_unit_1_alu_src));  // open: en
  // Probe on Data_1
  // Probe on Data_2
  ALU_12_bit alu_12_bit_1 (
    .Result(Result___Addr_Lw___Sw), .Zero_Detector(Zero_Detector), .A(Data_1), .B(Data_2),
    .C_in(control_unit_1_sub), .B_Invert(control_unit_1_sub), .ALU_Op(OP_Code), .C_overflow(C_overflow));
  // Probe on Store_Data
  or or_1 (or_1_out, Store, Load);
  // Probe on Result___Addr_Lw___Sw
  RAM #(.addrWidth(12), .dataWidth(12), .bus("separate")) ram_1 (
    .addr(Result___Addr_Lw___Sw), .din(Store_Data), .data(ram_1_data), .str(Store), .sel(or_1_out),
    .clk(Clock), .ld(Load), .clr(Reset_3_out));
  Button Reset_3 (.out(Reset_3_out));
  // Probe on Result___MEM_Data
  Multiplexer #(.width(12)) multiplexer_5 (
    .in0(Result___Addr_Lw___Sw), .in1(ram_1_data), .out(Result___MEM_Data), .sel(RAM_to_REG));  // open: en
  // Probe on Result___MEM_Data

  assign Jump_Address[8:0] = Jump___Target;
  assign Next_Inst_Address[11:9] = Jump_Address[11:9];
  assign RD_Imm = Jump___Target[2:0];
  assign RS = Jump___Target[8:6];
  assign RT = Jump___Target[5:3];

  // Notes on the sheet:
  //   contents of rom_1 (hex, n*v repeats v):
  //   408 415 c8a 449 e02 53 2cc 820 52e 606
  //   Immediate_Value
  //   BEQ
  //   Zobaer Ahammod Zamil
  //   ID: 2021796042
  //   Op_Code  |  Operations
  //   _____________________
  //   000       |        ADD
  //   001       |        SUB
  //   010       |       ADDI
  //   011       |       Load
  //   100       |       Store
  //   101       |       AND
  //   110       |       Beq
  //   111       |       Jump
endmodule

module Register_File_12_bit (
  input  Enable,
  input  Clock,
  input  Reset,
  input  [11:0] Write_Data,
  input  [2:0] RS,
  input  [2:0] RD,
  input  [2:0] RT,
  output [11:0] Read_Data_1,
  output [11:0] Read_Data_2
);

  wire and_1_out, and_2_out, and_3_out, and_4_out, and_5_out, and_6_out, and_7_out, and_8_out,
       decoder_1_out0, decoder_1_out1, decoder_1_out2, decoder_1_out3, decoder_1_out4, decoder_1_out5,
       decoder_1_out6, decoder_1_out7;
  wire [11:0] R0_q, R1_q, R2_q, R3_q, R4_q, R5_q, R6_q, R7_q;

  Decoder #(.select(3)) decoder_1 (
    .out0(decoder_1_out0), .out1(decoder_1_out1), .out2(decoder_1_out2), .out3(decoder_1_out3),
    .out4(decoder_1_out4), .out5(decoder_1_out5), .out6(decoder_1_out6), .out7(decoder_1_out7), .sel(RD));  // open: en
  // Probe on Write_Data
  and and_1 (and_1_out, decoder_1_out0, Enable);
  and and_2 (and_2_out, decoder_1_out1, Enable);
  and and_3 (and_3_out, decoder_1_out2, Enable);
  and and_4 (and_4_out, decoder_1_out3, Enable);
  and and_5 (and_5_out, decoder_1_out4, Enable);
  and and_6 (and_6_out, decoder_1_out5, Enable);
  and and_7 (and_7_out, decoder_1_out6, Enable);
  and and_8 (and_8_out, decoder_1_out7, Enable);
  Register #(.width(12)) R0 (.D(Write_Data), .en(and_1_out), .Q(R0_q), .clk(Clock), .clr(Reset));
  Register #(.width(12)) R1 (.D(Write_Data), .en(and_2_out), .Q(R1_q), .clk(Clock), .clr(Reset));
  Register #(.width(12)) R2 (.D(Write_Data), .en(and_3_out), .Q(R2_q), .clk(Clock), .clr(Reset));
  Register #(.width(12)) R3 (.D(Write_Data), .en(and_4_out), .Q(R3_q), .clk(Clock), .clr(Reset));
  Register #(.width(12)) R4 (.D(Write_Data), .en(and_5_out), .Q(R4_q), .clk(Clock), .clr(Reset));
  Register #(.width(12)) R5 (.D(Write_Data), .en(and_6_out), .Q(R5_q), .clk(Clock), .clr(Reset));
  Register #(.width(12)) R6 (.D(Write_Data), .en(and_7_out), .Q(R6_q), .clk(Clock), .clr(Reset));
  Register #(.width(12)) R7 (.D(Write_Data), .en(and_8_out), .Q(R7_q), .clk(Clock), .clr(Reset));
  // Probe on Read_Data_1
  Multiplexer #(.select(3), .width(12)) multiplexer_1 (
    .in0(R0_q), .in1(R1_q), .in2(R2_q), .in3(R3_q), .in4(R4_q), .in5(R5_q), .in6(R6_q), .in7(R7_q),
    .out(Read_Data_1), .sel(RS));  // open: en
  // Probe on Read_Data_2
  Multiplexer #(.select(3), .width(12)) multiplexer_2 (
    .in0(R0_q), .in1(R1_q), .in2(R2_q), .in3(R3_q), .in4(R4_q), .in5(R5_q), .in6(R6_q), .in7(R7_q),
    .out(Read_Data_2), .sel(RT));  // open: en
endmodule

module ALU_12_bit (
  input  [11:0] A,
  input  [11:0] B,
  input  C_in,
  input  B_Invert,
  input  [2:0] ALU_Op,
  output C_overflow,
  output [11:0] Result,
  output Zero_Detector
);

  wire [11:0] adder_1_out, and_1_out, multiplexer_1_out, not_1_out;

  // Probe on A
  // Probe on B
  assign not_1_out = ~B;  // NOT_Gate not_1, 12 bits wide
  Multiplexer #(.width(12)) multiplexer_1 (
    .in0(B), .in1(not_1_out), .out(multiplexer_1_out), .sel(B_Invert));  // open: en
  Adder #(.width(12)) adder_1 (.a(A), .b(multiplexer_1_out), .out(adder_1_out), .cin(C_in), .cout(C_overflow));
  assign and_1_out = A & multiplexer_1_out;  // AND_Gate and_1, 12 bits wide
  Multiplexer #(.select(3), .width(12)) multiplexer_2 (
    .in0(adder_1_out), .in1(adder_1_out), .in2(adder_1_out), .in3(adder_1_out), .in4(adder_1_out),
    .in5(adder_1_out), .in6(and_1_out), .in7(adder_1_out), .out(Result), .sel(ALU_Op));  // open: en
  // Probe on Result
  nor nor_1 (Zero_Detector, Result[0], Result[1], Result[2], Result[3], Result[4], Result[5], Result[6], Result[7], Result[8], Result[9], Result[10], Result[11]);
endmodule

module Control_Unit (
  input  [2:0] ALU_OP,
  output RT_RD,
  output Write_Enb,
  output ALU_Src,
  output Sub,
  output Load_enb,
  output Store_enb,
  output Jump_Control,
  output Beq_Control,
  output RAM_to_Reg
);

  Multiplexer #(.select(3)) multiplexer_1 (
    .in0(1'b1), .in1(1'b1), .in2(1'b0), .in3(1'b0), .in4(1'b0), .in5(1'b1), .in6(1'b0), .in7(1'b0),
    .out(RT_RD), .sel(ALU_OP));  // open: en
  Multiplexer #(.select(3)) multiplexer_2 (
    .in0(1'b1), .in1(1'b1), .in2(1'b1), .in3(1'b1), .in4(1'b0), .in5(1'b1), .in6(1'b0), .in7(1'b0),
    .out(Write_Enb), .sel(ALU_OP));  // open: en
  Multiplexer #(.select(3)) multiplexer_3 (
    .in0(1'b0), .in1(1'b0), .in2(1'b1), .in3(1'b1), .in4(1'b1), .in5(1'b0), .in6(1'b0), .in7(1'b0),
    .out(ALU_Src), .sel(ALU_OP));  // open: en
  Multiplexer #(.select(3)) multiplexer_4 (
    .in0(1'b0), .in1(1'b1), .in2(1'b0), .in3(1'b0), .in4(1'b0), .in5(1'b0), .in6(1'b1), .in7(1'b0),
    .out(Sub), .sel(ALU_OP));  // open: en
  Multiplexer #(.select(3)) multiplexer_5 (
    .in0(1'b0), .in1(1'b0), .in2(1'b0), .in3(1'b1), .in4(1'b0), .in5(1'b0), .in6(1'b0), .in7(1'b0),
    .out(Load_enb), .sel(ALU_OP));  // open: en
  Multiplexer #(.select(3)) multiplexer_6 (
    .in0(1'b0), .in1(1'b0), .in2(1'b0), .in3(1'b0), .in4(1'b1), .in5(1'b0), .in6(1'b0), .in7(1'b0),
    .out(Store_enb), .sel(ALU_OP));  // open: en
  Multiplexer #(.select(3)) multiplexer_7 (
    .in0(1'b0), .in1(1'b0), .in2(1'b0), .in3(1'b0), .in4(1'b0), .in5(1'b0), .in6(1'b0), .in7(1'b1),
    .out(Jump_Control), .sel(ALU_OP));  // open: en
  Multiplexer #(.select(3)) multiplexer_8 (
    .in0(1'b0), .in1(1'b0), .in2(1'b0), .in3(1'b0), .in4(1'b0), .in5(1'b0), .in6(1'b1), .in7(1'b0),
    .out(Beq_Control), .sel(ALU_OP));  // open: en
  Multiplexer #(.select(3)) multiplexer_9 (
    .in0(1'b0), .in1(1'b0), .in2(1'b0), .in3(1'b1), .in4(1'b0), .in5(1'b0), .in6(1'b0), .in7(1'b0),
    .out(RAM_to_Reg), .sel(ALU_OP));  // open: en
endmodule
